# Fritzing sketch СХема (saved by Fritzing 0.9.3b)
breadboards: 1

parts:
  Часть1 = Arduino Pro Mini v13
  YwRobot_Power_Supply1 = YwRobot Breadboard Power Supply [part_number=545043]
  J1 = Basic Servo
  Часть2 = Adafruit VL530X Time of Flight Distance Sensor [part_number="Adafruit #3317"]

nets:
  GND: Часть1.GND, YwRobot_Power_Supply1.GND#13, YwRobot_Power_Supply1.GND#14, J1.gnd, Часть2.GND
  N1: Часть1.VCC, YwRobot_Power_Supply1.VCC#5, YwRobot_Power_Supply1.VCC#6
  N2: Часть1.D13/SCK, Часть2.SDA
  N3: Часть1.D12/MISO, Часть2.SCL
  N4: Часть1.D2, J1.pulse
  VCC: YwRobot_Power_Supply1.VCC#9, YwRobot_Power_Supply1.VCC#10, J1.vcc, Часть2.VCC
  N5: YwRobot_Power_Supply1.GND#11, YwRobot_Power_Supply1.GND#12

custom parts:
  YwRobot Breadboard Power Supply: The YwRobot Breadboard Power Supply (MB-V2) has two power rails; they can be 5V or 3V3. Power to the module can be provided through the female USB socket or through the A10 (female) 2.1mm power jack.
  Adafruit VL530X Time of Flight Distance Sensor: The VL53L0X is a Time of Flight distance sensor like no other you've used! The sensor contains a very tiny invisible laser source, and a matching sensor. The VL53L0X can detect the "time of flight", or how long the light has taken to bounce back to the sensor. Since it uses a very narrow light source, it is good for determining distance of only the surface directly in front of it. Unlike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
